# Fritzing sketch SRC (saved by Fritzing 0.9.4)
breadboards: 1

parts:
  S9 = Pushbutton [package="[THT]"]
  S7 = Pushbutton [package="[THT]"]
  OLED_SCREEN = Grove OLED 128x96
  S6 = Pushbutton [package="[THT]"]
  WIZ820io1 = WIZ820io [part_number=WIZ820io]
  S10 = Pushbutton [package="[THT]"]
  S8 = Pushbutton [package="[THT]"]
  Teensy_3_1 = Teensy 3.1
  RG_encoder1 = SprkFn RG Encoder [package="DIP (Dual Inline) [THT]"]
  Reciever = mystery part, 4 pins [chip_label=?]

nets (from the breadboard view):
  N1: S9.Pin_1, S9.Pin_2, Teensy_3_1.D6
  GND: S9.Pin_3, S9.Pin_4, S7.Pin_3, S7.Pin_4, OLED_SCREEN.GND, S6.Pin_3, S6.Pin_4, WIZ820io1.GND, S10.Pin_3, S10.Pin_4, S8.Pin_3, S8.Pin_4, RG_encoder1.GND, RG_encoder1.C, Reciever.pin4
  N2: S7.Pin_1, S7.Pin_2, Teensy_3_1.D4
  VIN: OLED_SCREEN.VCC, WIZ820io1.VIN, Teensy_3_1.Vin
  N3: OLED_SCREEN.SDA, Teensy_3_1.A4/D18
  N4: OLED_SCREEN.SCL, Teensy_3_1.A5/D19
  N5: S6.Pin_1, S6.Pin_2, Teensy_3_1.D3
  N6: WIZ820io1.MOSI, Teensy_3_1.D11
  N7: WIZ820io1.SCLK, Teensy_3_1.D13
  N8: WIZ820io1.nSS, Teensy_3_1.D10
  N9: WIZ820io1.MISO, Teensy_3_1.D12
  N10: S10.Pin_1, S10.Pin_2, Teensy_3_1.D7
  N11: S8.Pin_1, S8.Pin_2, Teensy_3_1.D5
  N12: Teensy_3_1.D8, Reciever.pin2
  N13: Teensy_3_1.A0/D14, RG_encoder1.A
  N14: Teensy_3_1.A1/D15, RG_encoder1.B
  N15: Teensy_3_1.A2/D16, RG_encoder1.+G
  N16: Teensy_3_1.A7/D21, RG_encoder1.SW
  N17: Teensy_3_1.3V3, Reciever.pin1

custom parts:
  Pushbutton: A generic pushbutton.
  SprkFn RG Encoder: SparkFun RG Rotary Encoder
