# Fritzing sketch SRCtrans (saved by Fritzing 0.9.4)
breadboards: 1

parts:
  S9 = Pushbutton [package="[THT]"]
  S7 = Pushbutton [package="[THT]"]
  S6 = Pushbutton [package="[THT]"]
  S10 = Pushbutton [package="[THT]"]
  S8 = Pushbutton [package="[THT]"]
  Teensy_3_1 = Teensy 3.1
  LED1 = LED - 5mm [color="Red (633nm)" package="5 mm [THT]"]
  Transmitter = mystery part, 3 pins [chip_label=?]

nets:
  N1: S9.Pin_1, S9.Pin_2, Teensy_3_1.D5
  N2: S9.Pin_3, S9.Pin_4, S7.Pin_3, S7.Pin_4, S6.Pin_3, S6.Pin_4, S10.Pin_3, S10.Pin_4, S8.Pin_4, Teensy_3_1.GND, LED1.cathode, Transmitter.pin3
  N3: S7.Pin_1, S7.Pin_2, Teensy_3_1.D3
  N4: S6.Pin_1, S6.Pin_2, Teensy_3_1.D2
  N5: S10.Pin_1, S10.Pin_2, Teensy_3_1.D6
  N6: S8.Pin_1, S8.Pin_2, Teensy_3_1.D4
  N7: Teensy_3_1.D7, Transmitter.pin2
  N8: Teensy_3_1.D8, LED1.anode
  N9: Teensy_3_1.3V3, Transmitter.pin1

custom parts:
  Pushbutton: A generic pushbutton.
